# Fritzing sketch Data_Logger_xiao_internalRTC (saved by Fritzing 0.9.3b)
breadboards: 1

parts:
  Mod1 = seeeduino-xiao
  Bauteil2 = MicroSD Card Module

nets:
  N1: Mod1.D3, Bauteil2.CS
  N2: Mod1.D8, Bauteil2.SCK
  N3: Mod1.D9, Bauteil2.MISO
  N4: Mod1.D10, Bauteil2.MOSI
  3V3: Mod1.3V3, Bauteil2.VCC
  GND: Mod1.GND, Bauteil2.GND

notes:
  3.3 V
  5 V
  Batterie Anschluss

custom parts:
  seeeduino-xiao: Seeeduino XIAO processor board.
