# Fritzing sketch Data_Logger_xiao_internalRTC_withSensors (saved by Fritzing 0.9.3b)
breadboards: 1

parts:
  Mod1 = seeeduino-xiao
  Bauteil2 = MicroSD Card Module
  Bauteil3 = BME280 Breakout
  Capacitive_Soil_Moisture_Sensor1 = DFRobot Capacitive Soil Moisture Sensor V1.0 [part_number=SEN0193]

nets:
  N1: Mod1.D3, Bauteil2.CS
  N2: Mod1.D4, Bauteil3.SCK/SCL
  N3: Mod1.D5, Bauteil3.SDI/SDA
  N4: Mod1.D6, Capacitive_Soil_Moisture_Sensor1.A
  N5: Mod1.D7, Capacitive_Soil_Moisture_Sensor1.VCC
  N6: Mod1.D8, Bauteil2.SCK
  N7: Mod1.D9, Bauteil2.MISO
  N8: Mod1.D10, Bauteil2.MOSI
  3V3: Mod1.3V3, Bauteil2.VCC, Bauteil3.3.3V
  GND: Mod1.GND, Bauteil2.GND, Bauteil3.GND, Capacitive_Soil_Moisture_Sensor1.GND

notes:
  3.3 V
  3.3 V
  Batterie Anschluss

custom parts:
  seeeduino-xiao: Seeeduino XIAO processor board.
  DFRobot Capacitive Soil Moisture Sensor V1.0: DFRobot Capacitive Soil Moisture Sensor V1.0 This product measures soil moisture levels by capacitive sensing, rather than resistive sensing like other types of moisture sensor. It is made of a corrosion resistant material giving it a long service life. Insert it into soil and impress your friends with the real-time soil moisture data! The product includes an on-board voltage regulator which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
